# Fritzing sketch Lab_01 (saved by Fritzing 1.0.6)
breadboards: 1

parts:
  Part1 = Arduino Uno (Rev3)
  LED1 = smd LED [color="Red (633nm)" package="0603 [SMD]"]
  R1 = Resistor [tolerance=±5% resistance=220 package="2010 [SMD]"]

nets:
  N1: Part1.D13/SCK, R1.Pin_0
  N2: Part1.GND, LED1.cathode
  N3: LED1.anode, R1.Pin_1
