# Fritzing sketch Lab_02 (saved by Fritzing 1.0.6)
breadboards: 1

parts:
  R1 = Resistor [tolerance=±5% power=0.25W resistance=220 package=THT]
  LED2 = LED - 5mm [color="Red (633nm)" current=0.030A package="5 mm [THT]"]
  LED3 = LED - 5mm [color="Red (633nm)" current=0.030A package="5 mm [THT]"]
  LED4 = LED - 5mm [color="Red (633nm)" current=0.030A package="5 mm [THT]"]
  LED5 = LED - 5mm [color="Red (633nm)" current=0.030A package="5 mm [THT]"]
  LED6 = LED - 5mm [color="Red (633nm)" current=0.030A package="5 mm [THT]"]
  LED7 = LED - 5mm [color="Red (633nm)" current=0.030A package="5 mm [THT]"]
  LED8 = LED - 5mm [color="Red (633nm)" current=0.030A package="5 mm [THT]"]
  R2 = Resistor [tolerance=±5% power=0.25W resistance=220 package=THT]
  R3 = Resistor [tolerance=±5% power=0.25W resistance=220 package=THT]
  R4 = Resistor [tolerance=±5% power=0.25W resistance=220 package=THT]
  R5 = Resistor [tolerance=±5% power=0.25W resistance=220 package=THT]
  R6 = Resistor [tolerance=±5% power=0.25W resistance=220 package=THT]
  R7 = Resistor [tolerance=±5% power=0.25W resistance=220 package=THT]
  R8 = Resistor [tolerance=±5% power=0.25W resistance=220 package=THT]
  Part1 = Arduino Uno (Rev3)
  LED9 = LED - 5mm [color="Red (633nm)" current=0.030A package="5 mm [THT]"]

nets:
  N1: R1.Pin_0, R2.Pin_0, R3.Pin_0, R4.Pin_0, R5.Pin_0, R6.Pin_0, R7.Pin_0, R8.Pin_0, Part1.GND
  N2: R1.Pin_1, LED9.cathode
  N3: LED2.cathode, R2.Pin_1
  N4: LED2.anode, Part1.D3_PWM
  N5: LED3.cathode, R3.Pin_1
  N6: LED3.anode, Part1.D4
  N7: LED4.cathode, R4.Pin_1
  N8: LED4.anode, Part1.D5_PWM
  N9: LED5.cathode, R5.Pin_1
  N10: LED5.anode, Part1.D6_PWM
  N11: LED6.cathode, R6.Pin_1
  N12: LED6.anode, Part1.D7
  N13: LED7.cathode, R7.Pin_1
  N14: LED7.anode, Part1.D8
  N15: LED8.cathode, R8.Pin_1
  N16: LED8.anode, Part1.D9_PWM
  N17: Part1.D2, LED9.anode

// code stored in the sketch: Untitled2.ino
//ERIC MANUEL R MANZANERO 
//BSCpE 3A


//variable to control the speed
const int time = 100;


void setup() {
  // put your setup code here, to run once:
  //Initialize pins 2 through 9 as OUTPUT using loop
  for (int pin = 2; pin <= 9; pin++){
    pinMode(pin, OUTPUT);
  }
}


void loop() {
  // put your main code here, to run repeatedly:
  //Pattern 1: The "Chase" (Left to Right)
  for (int pin = 2; pin <= 9; pin++){
    digitalWrite(pin, HIGH); //Turn LED on
    delay(time); //Speed of the "dance"
    digitalWrite(pin, LOW); //Turn LED off
    }


  // Pattern 2: The "Return" (Right to Left)
  for (int pin = 9; pin >= 2; pin--){
    digitalWrite(pin, HIGH); //Turn LED on
    delay(time); //Speed of the "dance"
    digitalWrite(pin, LOW); //Turn LED off
    }
}
