# Fritzing sketch Lab_03_3X3_LED_Matrix_Control_with_Arduino (saved by Fritzing 1.0.6)
breadboards: 1

parts:
  LED1 = LED - 5mm [color="Red (633nm)" current=0.030A package="5 mm [THT]"]
  LED2 = LED - 5mm [color="Red (633nm)" current=0.030A package="5 mm [THT]"]
  LED3 = LED - 5mm [color="Red (633nm)" current=0.030A package="5 mm [THT]"]
  LED4 = LED - 5mm [color="Red (633nm)" current=0.030A package="5 mm [THT]"]
  LED5 = LED - 5mm [color="Red (633nm)" current=0.030A package="5 mm [THT]"]
  LED6 = LED - 5mm [color="Red (633nm)" current=0.030A package="5 mm [THT]"]
  LED7 = LED - 5mm [color="Red (633nm)" current=0.030A package="5 mm [THT]"]
  LED8 = LED - 5mm [color="Red (633nm)" current=0.030A package="5 mm [THT]"]
  LED9 = LED - 5mm [color="Red (633nm)" current=0.030A package="5 mm [THT]"]
  R1 = Resistor [tolerance=±5% power=0.25W resistance=330 package=THT]
  R2 = Resistor [tolerance=±5% power=0.25W resistance=330 package=THT]
  R3 = Resistor [tolerance=±5% power=0.25W resistance=330 package=THT]
  Part1 = Arduino Uno (Rev3)

nets:
  N1: LED1.cathode, LED4.cathode, LED7.cathode, R3.Pin_0
  N2: LED1.anode, LED2.anode, LED3.anode, Part1.D2
  N3: LED2.cathode, LED5.cathode, LED8.cathode, R2.Pin_0
  N4: LED3.cathode, LED6.cathode, LED9.cathode, R1.Pin_0
  N5: LED4.anode, LED5.anode, LED6.anode, Part1.D3_PWM
  N6: LED7.anode, LED8.anode, LED9.anode, Part1.D4
  N7: R1.Pin_1, Part1.D5_PWM
  N8: R2.Pin_1, Part1.D6_PWM
  N9: R3.Pin_1, Part1.D7
