# Fritzing sketch CoinSorter (saved by Fritzing 0.9.5d)
breadboards: 1

parts:
  M1 = fc-51 [package=THT]
  M2 = fc-51 [package=THT]
  M3 = fc-51 [package=THT]
  M4 = fc-51 [package=THT]
  Part1 = Arduino Nano (Rev3.0)
  BREAKOUT1 = ULN2003A breakout board
  MOTOR1 = 28BYJ-48 Stepper Motor
  GLCD_128x1 = 128 x 64 Graphic LCD  # not connected
  LCD1 = LCD screen  # not connected

nets:
  N1: M1.pin1, Part1.D7
  N2: M1.pin2, M2.pin2, M3.pin2, M4.pin2, Part1.GND, BREAKOUT1.0V
  5V: M1.pin3, M2.pin3, M3.pin3, M4.pin3, Part1.5V, BREAKOUT1.+5V
  N3: M2.pin1, Part1.D4
  N4: M3.pin1, Part1.D5
  N5: M4.pin1, Part1.D6
  N6: BREAKOUT1.RED_wire, MOTOR1.RED
  N7: BREAKOUT1.ORANGE_wire, MOTOR1.ORANGE
  N8: BREAKOUT1.YELLOW_wire, MOTOR1.YELLOW
  N9: BREAKOUT1.PINK_wire, MOTOR1.PINK
  N10: BREAKOUT1.BLUE_wire, MOTOR1.BLUE

custom parts:
  ULN2003A breakout board: ULN2003A 7-way Darlington Transistor Driver on breakoutboard
