# Fritzing sketch Coin Sorter Schematic (saved by Fritzing 0.9.5d)
breadboards: 1

parts:
  Part1 = LCD1602-I2C
  Part3 = Arduino Uno (Rev3)
  M1 = fc-51 [package=THT]
  S1 = Pushbutton [package="[SMD]"]
  S2 = Pushbutton [package="[SMD]"]
  S3 = Pushbutton [package="[SMD]"]
  S4 = Pushbutton [package="[SMD]"]
  S5 = Pushbutton [package="[SMD]"]
  S6 = Pushbutton [package="[SMD]"]
  M2 = fc-51 [package=THT]
  M3 = fc-51 [package=THT]
  M4 = fc-51 [package=THT]
  BREAKOUT3 = ULN2003A breakout board
  MOTOR3 = 28BYJ-48 Stepper Motor

nets:
  GND: Part1.GND, Part3.GND, M1.pin2, S1.Pin_1, S1.Pin_2, S2.Pin_1, S2.Pin_2, S3.Pin_1, S3.Pin_2, S4.Pin_1, S4.Pin_2, S5.Pin_1, S5.Pin_2, S6.Pin_1, S6.Pin_2, M2.pin2, M3.pin2, M4.pin2
  VCC: Part1.VCC, Part3.5V, M1.pin3, M2.pin3, M3.pin3, M4.pin3
  N1: Part1.SDA, Part3.A4/SDA
  N2: Part1.SCL, Part3.A5/SCL
  N3: Part3.D8, S5.Pin_3, S5.Pin_4
  N4: Part3.D9_PWM, S6.Pin_3, S6.Pin_4
  N5: Part3.D10_PWM/SS, S3.Pin_3, S3.Pin_4
  N6: Part3.D11_PWM/MOSI, S4.Pin_3, S4.Pin_4
  N7: Part3.D12/MISO, S2.Pin_3, S2.Pin_4
  N8: Part3.D13/SCK, S1.Pin_3, S1.Pin_4
  N9: Part3.D0/RX, BREAKOUT3.In_1
  N10: Part3.D1/TX, BREAKOUT3.In_2
  N11: Part3.D2, BREAKOUT3.In_3
  N12: Part3.D3_PWM, BREAKOUT3.In_4
  N13: Part3.D4, M1.pin1
  N14: Part3.D5_PWM, M4.pin1
  N15: Part3.D6_PWM, M3.pin1
  N16: Part3.D7, M2.pin1
  N17: BREAKOUT3.RED_wire, MOTOR3.RED
  N18: BREAKOUT3.ORANGE_wire, MOTOR3.ORANGE
  N19: BREAKOUT3.YELLOW_wire, MOTOR3.YELLOW
  N20: BREAKOUT3.PINK_wire, MOTOR3.PINK
  N21: BREAKOUT3.BLUE_wire, MOTOR3.BLUE

notes:
  Sensor for one peso
  Sensor for five peso
  Sensor for ten peso
  Sensor for twenty peso
  Button for reset
  total
  One
  Five
  Ten
  Twenty
  Connected to 12 V DC

custom parts:
  LCD1602-I2C: A standard character display, usually with 2x16 characters. Comes in many colors with LCM1602 IIC attached.
  ULN2003A breakout board: ULN2003A 7-way Darlington Transistor Driver on breakoutboard
