# Fritzing sketch Stepper_motor (saved by Fritzing 0.9.5d)

parts:
  Part3 = Arduino Uno (Rev3)
  BREAKOUT2 = ULN2003A breakout board
  MOTOR2 = 28BYJ-48 Stepper Motor

nets:
  N1: Part3.D8, BREAKOUT2.In_1
  N2: Part3.D9_PWM, BREAKOUT2.In_2
  N3: Part3.D10_PWM/SS, BREAKOUT2.In_3
  N4: Part3.D11_PWM/MOSI, BREAKOUT2.In_4
  N5: BREAKOUT2.RED_wire, MOTOR2.RED
  N6: BREAKOUT2.ORANGE_wire, MOTOR2.ORANGE
  N7: BREAKOUT2.YELLOW_wire, MOTOR2.YELLOW
  N8: BREAKOUT2.PINK_wire, MOTOR2.PINK
  N9: BREAKOUT2.BLUE_wire, MOTOR2.BLUE

notes:
  Connected to 12 V DC

custom parts:
  ULN2003A breakout board: ULN2003A 7-way Darlington Transistor Driver on breakoutboard
