# Fritzing sketch Tutorial_05 (saved by Fritzing 1.0.6)
breadboards: 1

parts:
  LED1 = LED - 5mm [color="Red (633nm)" current=0.030A package="5 mm [THT]"]
  LED2 = LED - 5mm [color="Red (633nm)" current=0.030A package="5 mm [THT]"]
  LED3 = LED - 5mm [color="Red (633nm)" current=0.030A package="5 mm [THT]"]
  LED4 = LED - 5mm [color="Red (633nm)" current=0.030A package="5 mm [THT]"]
  R1 = Resistor [tolerance=±5% power=0.25W resistance=220 package=THT]
  R2 = Resistor [tolerance=±5% power=0.25W resistance=220 package=THT]
  R3 = Resistor [tolerance=±5% power=0.25W resistance=220 package=THT]
  R4 = Resistor [tolerance=±5% power=0.25W resistance=220 package=THT]
  Part1 = Arduino Uno (Rev3)

nets:
  N1: LED1.cathode, R1.Pin_1
  N2: LED1.anode, Part1.D11_PWM/MOSI
  N3: LED2.cathode, R2.Pin_1
  N4: LED2.anode, Part1.D10_PWM/SS
  N5: LED3.cathode, R3.Pin_1
  N6: LED3.anode, Part1.D9_PWM
  N7: LED4.cathode, R4.Pin_1
  N8: LED4.anode, Part1.D8
  N9: R1.Pin_0, R2.Pin_0, R3.Pin_0, R4.Pin_0, Part1.GND
