# Fritzing sketch Tutorial_10_analogRead (saved by Fritzing 1.0.6)
breadboards: 1

parts:
  R1 = Resistor [tolerance=±5% power=0.25W resistance=220 package=THT]
  R2 = Resistor [tolerance=±5% power=0.25W resistance=330 package=THT]
  Part1 = Arduino Uno (Rev3)

nets:
  N1: R1.Pin_0, Part1.5V
  N2: R1.Pin_1, R2.Pin_1, Part1.A0
  N3: R2.Pin_0, Part1.GND

notes:
  330 Ohm
  220 Ohm
  Calculations:
  V = IR
  I = V/R
  R = 220 + 330
  V = 5
  I = V/R
  = 5/550
  = 9.09mA
  V1 = 9.09mA x 220
  = 2 V
  V2 = 9.09mA x 330
  = 3V
